// Logisim project mux.circ as structural Verilog: 1 circuit, main circuit mux 2x1
module mux_2x1 (
  input  in_1,
  input  in_2,
  input  in_3
);

  wire and_1_out, and_2_out, or_1_out;

  and and_1 (and_1_out, in_1, ~in_2);  // AND_Gate
  and and_2 (and_2_out, in_1, in_3);
  or or_1 (or_1_out, and_1_out, and_2_out);
  Button s ();  // open: out
endmodule
